// Logisim project Banco de Registradores.circ as structural Verilog: 1 circuit, main circuit Banco de Registradores
module Banco_de_Registradores (
  input  [7:0] in_1,
  input  CLEAR,
  input  in_3,
  input  [3:0] in_4,
  input  [3:0] in_5,
  input  [3:0] in_6,
  output [7:0] out_7,
  output [7:0] out_8
);

  wire clock_1_out, decoder_1_out0, decoder_1_out1, decoder_1_out2, decoder_1_out3, decoder_1_out4,
       decoder_1_out5, decoder_1_out6, decoder_1_out7, decoder_1_out8, decoder_1_out9, decoder_1_out10,
       decoder_1_out11, decoder_1_out12, decoder_1_out13, decoder_1_out14, decoder_1_out15;
  wire [7:0] RE10_q, REG0_q, REG1_q, REG2_q, REG3_q, REG4_q, REG5_q, REG6_q, REG7_q, REG8_q, REG9_q, REG11_q,
       REG12_q, REG13_q, REG14_q, REG15_q;

  Clock clock_1 (.out(clock_1_out));
  Register REG15 (.D(in_1), .en(decoder_1_out15), .Q(REG15_q), .clk(clock_1_out), .clr(CLEAR));
  Multiplexer #(.select(4), .width(8), .enable("false")) multiplexer_1 (
    .in0(REG0_q), .in1(REG1_q), .in2(REG2_q), .in3(REG3_q), .in4(REG4_q), .in5(REG5_q), .in6(REG6_q),
    .in7(REG7_q), .in8(REG8_q), .in9(REG9_q), .in10(RE10_q), .in11(REG11_q), .in12(REG12_q), .in13(REG13_q),
    .in14(REG14_q), .in15(REG15_q), .out(out_7), .sel(in_5));
  Multiplexer #(.select(4), .width(8), .enable("false")) multiplexer_2 (
    .in0(REG0_q), .in1(REG1_q), .in2(REG2_q), .in3(REG3_q), .in4(REG4_q), .in5(REG5_q), .in6(REG6_q),
    .in7(REG7_q), .in8(REG8_q), .in9(REG9_q), .in10(RE10_q), .in11(REG11_q), .in12(REG12_q), .in13(REG13_q),
    .in14(REG14_q), .in15(REG15_q), .out(out_8), .sel(in_6));
  Register REG14 (.D(in_1), .en(decoder_1_out14), .Q(REG14_q), .clk(clock_1_out), .clr(CLEAR));
  Register REG12 (.D(in_1), .en(decoder_1_out12), .Q(REG12_q), .clk(clock_1_out), .clr(CLEAR));
  Register REG13 (.D(in_1), .en(decoder_1_out13), .Q(REG13_q), .clk(clock_1_out), .clr(CLEAR));
  Register REG11 (.D(in_1), .en(decoder_1_out11), .Q(REG11_q), .clk(clock_1_out), .clr(CLEAR));
  Register RE10 (.D(in_1), .en(decoder_1_out10), .Q(RE10_q), .clk(clock_1_out), .clr(CLEAR));
  Register REG9 (.D(in_1), .en(decoder_1_out9), .Q(REG9_q), .clk(clock_1_out), .clr(CLEAR));
  Register REG8 (.D(in_1), .en(decoder_1_out8), .Q(REG8_q), .clk(clock_1_out), .clr(CLEAR));
  Register REG7 (.D(in_1), .en(decoder_1_out7), .Q(REG7_q), .clk(clock_1_out), .clr(CLEAR));
  Register REG6 (.D(in_1), .en(decoder_1_out6), .Q(REG6_q), .clk(clock_1_out), .clr(CLEAR));
  Register REG4 (.D(in_1), .en(decoder_1_out4), .Q(REG4_q), .clk(clock_1_out), .clr(CLEAR));
  Register REG5 (.D(in_1), .en(decoder_1_out5), .Q(REG5_q), .clk(clock_1_out), .clr(CLEAR));
  Register REG3 (.D(in_1), .en(decoder_1_out3), .Q(REG3_q), .clk(clock_1_out), .clr(CLEAR));
  Register REG2 (.D(in_1), .en(decoder_1_out2), .Q(REG2_q), .clk(clock_1_out), .clr(CLEAR));
  Register REG0 (.D(in_1), .en(decoder_1_out0), .Q(REG0_q), .clk(clock_1_out), .clr(CLEAR));
  Register REG1 (.D(in_1), .en(decoder_1_out1), .Q(REG1_q), .clk(clock_1_out), .clr(CLEAR));
  Decoder #(.select(4)) decoder_1 (
    .out0(decoder_1_out0), .out1(decoder_1_out1), .out2(decoder_1_out2), .out3(decoder_1_out3),
    .out4(decoder_1_out4), .out5(decoder_1_out5), .out6(decoder_1_out6), .out7(decoder_1_out7),
    .out8(decoder_1_out8), .out9(decoder_1_out9), .out10(decoder_1_out10), .out11(decoder_1_out11),
    .out12(decoder_1_out12), .out13(decoder_1_out13), .out14(decoder_1_out14), .out15(decoder_1_out15),
    .sel(in_4), .en(in_3));
endmodule
