// Logisim project tarefa 5.circ as structural Verilog: 1 circuit, main circuit main
module main (
  input  W,
  input  reset,
  output Z
);

  wire and_1_out, and_2_out, clock_1_out, d_ff_1_qn, d_ff_2_q, d_ff_2_qn, or_1_out;

  or or_1 (or_1_out, Z, d_ff_2_q);
  Clock clock_1 (.out(clock_1_out));
  and and_1 (and_1_out, or_1_out, W);
  and and_2 (and_2_out, d_ff_1_qn, W, d_ff_2_qn);
  D_Flip_Flop d_ff_1 (.clk(clock_1_out), .D(and_1_out), .Q(Z), .Qn(d_ff_1_qn), .reset(reset));  // open: preset, en
  D_Flip_Flop d_ff_2 (
    .clk(clock_1_out), .D(and_2_out), .Q(d_ff_2_q), .Qn(d_ff_2_qn), .reset(reset));  // open: preset, en
endmodule
