// Logisim project Swap R2-R1.circ as structural Verilog: 2 circuits, main circuit main
module main (
  input  RESET,
  input  CLOCK,
  input  W,
  output C1,
  output H1,
  output C2,
  output H2,
  output C3,
  output H3,
  output Done
);

  wire and_1_out, and_2_out, and_3_out, d_ff_1_q, d_ff_1_qn, d_ff_2_q, d_ff_2_qn, or_1_out, or_2_out;

  and and_1 (and_1_out, d_ff_2_q, d_ff_1_qn);
  and and_2 (and_2_out, d_ff_1_q, d_ff_2_qn);
  and and_3 (and_3_out, d_ff_2_qn, W);
  or or_1 (or_1_out, and_1_out, and_2_out);
  or or_2 (or_2_out, and_2_out, and_3_out);
  D_Flip_Flop d_ff_1 (.clk(CLOCK), .D(or_1_out), .Q(d_ff_1_q), .Qn(d_ff_1_qn), .reset(RESET));  // open: preset, en
  D_Flip_Flop d_ff_2 (.clk(CLOCK), .D(or_2_out), .Q(d_ff_2_q), .Qn(d_ff_2_qn), .reset(RESET));  // open: preset, en
  and and_4 (C1, d_ff_1_q, d_ff_2_q);
  and and_5 (C3, d_ff_1_qn, d_ff_2_q);
  and and_6 (C2, d_ff_1_q, d_ff_2_qn);

  assign Done = C1;
  assign H1 = C2;
  assign H2 = C3;
  assign H3 = C1;
endmodule

module circuito_de_controle (
  input  RESET,
  input  W,
  output [7:0] out_3,
  output Done
);

  wire clock_1_out, main_1_c1, main_1_c2, main_1_c3, main_1_h1, main_1_h2, main_1_h3;
  wire [7:0] R1_q, R2_q, R3_q;

  Clock clock_1 (.out(clock_1_out));
  Register R1 (.D(out_3), .en(main_1_c1), .Q(R1_q), .clk(clock_1_out), .clr(RESET));
  assign out_3 = main_1_h1 ? R1_q : 8'bz;  // Controlled_Buffer controlled_buffer_1
  Register R2 (.D(out_3), .en(main_1_c2), .Q(R2_q), .clk(clock_1_out), .clr(RESET));
  main main_1 (
    .RESET(RESET), .CLOCK(clock_1_out), .W(W), .C1(main_1_c1), .H1(main_1_h1), .C2(main_1_c2),
    .H2(main_1_h2), .C3(main_1_c3), .H3(main_1_h3), .Done(Done));
  Register R3 (.D(out_3), .en(main_1_c3), .Q(R3_q), .clk(clock_1_out), .clr(RESET));
  assign out_3 = main_1_h2 ? R2_q : 8'bz;  // Controlled_Buffer controlled_buffer_2
  assign out_3 = main_1_h3 ? R3_q : 8'bz;  // Controlled_Buffer controlled_buffer_3
endmodule
