// Logisim project Circuito Somador Sequencial.circ as structural Verilog: 2 circuits, main circuit main
module main (
  input  Inicio,
  input  [3:0] Qnt__de_Valores,
  input  [7:0] Valores,
  input  Reset,
  output Overflow,
  output [7:0] out_6
);

  wire circuito_somador_sequencial_1_pronto, clock_1_out;

  Clock clock_1 (.out(clock_1_out));
  Circuito_Somador_Sequencial circuito_somador_sequencial_1 (
    .Inicio(Inicio), .Qnt_de_Valores(Qnt__de_Valores), .Valores(Valores), .Clock(clock_1_out), .Reset(Reset),
    .Pronto(circuito_somador_sequencial_1_pronto), .Overflow(Overflow), .Soma(out_6));
  LED led_1 (.in(circuito_somador_sequencial_1_pronto));

  // Notes on the sheet:
  //   Clock
  //   Pronto
  //   Soma
endmodule

module Circuito_Somador_Sequencial (
  input  Inicio,
  input  [3:0] Qnt_de_Valores,
  input  Clock,
  input  Reset,
  input  [7:0] Valores,
  output Pronto,
  output Overflow,
  output [7:0] Soma
);

  wire and_1_out, and_2_out, and_3_out, and_4_out, and_5_out, and_6_out, and_8_out, not_1_out, not_2_out,
       not_3_out, or_1_out, or_2_out, or_3_out, Q0_q, Q0_qn, Q1_q, Q1_qn, S;
  wire [3:0] counter_1_q;
  wire [7:0] adder_1_out, register_1_q, register_2_q;

  not not_1 (not_1_out, not_2_out);
  and and_1 (and_1_out, Inicio, Q1_qn);
  and and_2 (and_2_out, Inicio, not_1_out, Q0_q);
  or or_1 (or_1_out, and_1_out, and_2_out, and_3_out);
  and and_3 (and_3_out, Inicio, not_2_out, Q0_qn);
  and and_4 (and_4_out, Inicio, not_1_out, Q1_q);
  and and_5 (and_5_out, Inicio, Q0_qn, Q1_q);
  or or_2 (or_2_out, and_4_out, and_5_out, and_6_out);
  and and_6 (and_6_out, Inicio, not_2_out, Q1_qn);
  D_Flip_Flop Q1 (.clk(Clock), .D(or_1_out), .Q(Q1_q), .Qn(Q1_qn), .reset(Reset));  // open: preset, en
  D_Flip_Flop Q0 (.clk(Clock), .D(or_2_out), .Q(Q0_q), .Qn(Q0_qn), .reset(Reset));  // open: preset, en
  and and_7 (S, Q1_q, Q0_q);
  not not_2 (not_2_out, or_3_out);
  Register register_1 (.D(Valores), .Q(register_1_q), .clk(Clock), .clr(Reset));  // open: en
  Counter #(.width(4), .max('hf)) counter_1 (
    .load(Inicio), .D(Qnt_de_Valores), .count(or_3_out), .Q(counter_1_q), .clk(Clock), .clr(Reset));  // open: carry
  Register register_2 (.D(adder_1_out), .Q(register_2_q), .clk(Clock), .clr(not_3_out));  // open: en
  Adder adder_1 (.a(register_2_q), .b(register_1_q), .out(adder_1_out), .cout(Overflow));  // open: cin
  not not_3 (not_3_out, or_3_out);
  or or_3 (or_3_out, counter_1_q[0], counter_1_q[1], counter_1_q[2], counter_1_q[3]);
  and and_8 (and_8_out, or_3_out, S);
  not not_4 (Pronto, S);
  Register register_3 (.D(adder_1_out), .en(and_8_out), .Q(Soma), .clk(Clock), .clr(Reset));
  LED led_1 (.in(Pronto));

  // Other names for the same wires on the sheet: C = Clock; I = Inicio; O = Overflow; Q[3:0] = Qnt_de_Valores;
  //   R = Reset; V[7:0] = Valores

  // Notes on the sheet:
  //   Pronto
  //   Overflow
endmodule
