// Logisim project Circuito Sequencial.circ as structural Verilog: 2 circuits, main circuit main
module main (
  input  Inicio,
  input  Reset,
  input  [3:0] Qnt_de_Valores,
  input  [7:0] Valores,
  output [7:0] Soma
);

  wire and_1_out, C, not_1_out, not_2_out, not_3_out, O, or_1_out, S;
  wire [3:0] counter_1_q;
  wire [7:0] adder_1_out, register_1_q, register_2_q;

  Clock Clock (.out(C));
  not not_1 (not_1_out, or_1_out);
  Circuito_Sequencial circuito_sequencial_1 (.Clock(C), .Reset(Reset), .I(Inicio), .C(not_1_out), .S(S));
  LED led_1 (.in(not_2_out));
  not not_2 (not_2_out, S);
  LED led_2 (.in(O));
  Counter #(.width(4), .max('hf)) counter_1 (
    .load(Inicio), .D(Qnt_de_Valores), .count(or_1_out), .Q(counter_1_q), .clk(C), .clr(Reset));  // open: carry
  Register register_1 (.D(Valores), .Q(register_1_q), .clk(C), .clr(Reset));  // open: en
  Adder adder_1 (.a(register_2_q), .b(register_1_q), .out(adder_1_out), .cout(O));  // open: cin
  not not_3 (not_3_out, or_1_out);
  or or_1 (or_1_out, counter_1_q[0], counter_1_q[1], counter_1_q[2], counter_1_q[3]);
  Register register_2 (.D(adder_1_out), .Q(register_2_q), .clk(C), .clr(not_3_out));  // open: en
  Register register_3 (.D(adder_1_out), .en(and_1_out), .Q(Soma), .clk(C), .clr(Reset));
  and and_1 (and_1_out, or_1_out, S);

  // Other names for the same wires on the sheet: I = Inicio; Q[3:0] = Qnt_de_Valores; R = Reset; V[7:0] = Valores

  // Notes on the sheet:
  //   Pronto
  //   Overflow
endmodule

module Circuito_Sequencial (
  input  Clock,
  input  Reset,
  input  I,
  input  C,
  output S
);

  wire and_1_out, and_2_out, and_3_out, and_4_out, and_5_out, and_6_out, D0_q, D0_qn, D1_q, D1_qn, not_1_out,
       or_1_out, or_2_out;

  not not_1 (not_1_out, C);
  and and_1 (and_1_out, I, D1_qn);
  and and_2 (and_2_out, I, not_1_out, D0_q);
  and and_3 (and_3_out, I, C, D0_qn);
  and and_4 (and_4_out, I, not_1_out, D1_q);
  and and_5 (and_5_out, I, D0_qn, D1_q);
  and and_6 (and_6_out, I, C, D1_qn);
  D_Flip_Flop D1 (.clk(Clock), .D(or_1_out), .Q(D1_q), .Qn(D1_qn), .reset(Reset));  // open: preset, en
  or or_1 (or_1_out, and_1_out, and_2_out, and_3_out);
  D_Flip_Flop D0 (.clk(Clock), .D(or_2_out), .Q(D0_q), .Qn(D0_qn), .reset(Reset));  // open: preset, en
  or or_2 (or_2_out, and_4_out, and_5_out, and_6_out);
  and and_7 (S, D1_q, D0_q);
endmodule
