// Logisim project Exem.circ as structural Verilog: 2 circuits, main circuit main
module main (
  input  [3:0] Qtd_soma,
  input  CLK,
  input  RESET,
  input  INICIO,
  input  [7:0] Entrada_soma,
  output Pronto,
  output [3:0] out_7,
  output [7:0] Resultado,
  output [7:0] out_9,
  output [7:0] out_10,
  output Overflow
);

  wire and_1_out, and_2_out, and_3_out, and_4_out, and_5_out, and_7_out, cont, not_1_out, not_2_out,
       not_3_out, or_1_out, or_2_out, Q0_q, Q0_qn, Q1_q, Q1_qn;
  wire [7:0] register_1_q;

  not not_1 (not_1_out, cont);
  and and_1 (and_1_out, INICIO, cont, Q0_qn);
  and and_2 (and_2_out, INICIO, Q1_q, Q0_qn);
  and and_3 (and_3_out, INICIO, not_1_out, Q1_qn, Q0_q);
  and and_4 (and_4_out, INICIO, Q1_qn, Q0_q);
  and and_5 (and_5_out, INICIO, not_1_out, Q1_q, Q0_qn);
  Register register_1 (.D(Entrada_soma), .Q(register_1_q), .clk(CLK), .clr(RESET));  // open: en
  or or_1 (or_1_out, and_4_out, and_5_out);
  Adder adder_1 (.a(out_9), .b(register_1_q), .out(out_10), .cout(Overflow));  // open: cin
  or or_2 (or_2_out, and_1_out, and_2_out, and_3_out);
  Counter #(.width(4), .max('hf)) counter_1 (
    .load(INICIO), .D(Qtd_soma), .count(cont), .Q(out_7), .clk(CLK), .clr(RESET));  // open: carry
  D_Flip_Flop Q0 (.clk(CLK), .D(or_2_out), .Q(Q0_q), .Qn(Q0_qn), .reset(RESET));  // open: preset, en
  D_Flip_Flop Q1 (.clk(CLK), .D(or_1_out), .Q(Q1_q), .Qn(Q1_qn), .reset(RESET));  // open: preset, en
  or or_3 (cont, out_7[3], out_7[2], out_7[1], out_7[0]);
  not not_2 (not_2_out, cont);
  and and_6 (Pronto, Q0_q, Q1_q);
  Register register_2 (.D(out_10), .Q(out_9), .clk(CLK), .clr(not_2_out));  // open: en
  not not_3 (not_3_out, Pronto);
  Register register_3 (.D(out_10), .en(and_7_out), .Q(Resultado), .clk(CLK), .clr(RESET));
  and and_7 (and_7_out, not_3_out, cont);

  // Other names for the same wires on the sheet: c = CLK; i = INICIO; r = RESET; s = Pronto
endmodule

module somador_acumulador (
  input  [3:0] Qtd_Soma,
  input  CLK,
  input  Reset,
  input  \Início ,
  input  [7:0] Entrada_soma,
  output Fim_da_soma,
  output [3:0] cont,
  output [7:0] Resultado,
  output [7:0] out_9,
  output Overflow
);

  main main_1 (
    .Qtd_soma(Qtd_Soma), .CLK(CLK), .RESET(Reset), .INICIO(\Início ), .Entrada_soma(Entrada_soma),
    .Overflow(Overflow), .Pronto(Fim_da_soma), .out_7(cont), .Resultado(Resultado), .out_10(out_9));  // open: out_9
endmodule
