// Logisim project somador-subtrator.circ as structural Verilog: 3 circuits, main circuit Somador/Subtrator
module Somador (
  input  A0,
  input  B0,
  input  A1,
  input  B1,
  input  A2,
  input  B2,
  input  A3,
  input  B3,
  input  C,
  output S0,
  output S1,
  output S2,
  output S3,
  output Carry
);

  wire and_1_out, and_2_out, and_3_out, and_4_out, and_5_out, and_6_out, and_7_out, and_8_out, or_1_out,
       or_2_out, or_3_out, xor_1_out, xor_3_out, xor_5_out, xor_7_out;

  xor xor_1 (xor_1_out, B0, A0);
  xor xor_2 (S0, xor_1_out, C);
  and and_1 (and_1_out, xor_1_out, C);
  and and_2 (and_2_out, B0, B0);
  or or_1 (or_1_out, and_1_out, and_2_out);
  xor xor_3 (xor_3_out, B1, A1);
  xor xor_4 (S1, xor_3_out, or_1_out);
  and and_3 (and_3_out, xor_3_out, or_1_out);
  and and_4 (and_4_out, B1, B1);
  or or_2 (or_2_out, and_3_out, and_4_out);
  xor xor_5 (xor_5_out, B2, A2);
  xor xor_6 (S2, xor_5_out, or_2_out);
  and and_5 (and_5_out, xor_5_out, or_2_out);
  and and_6 (and_6_out, B2, B2);
  or or_3 (or_3_out, and_5_out, and_6_out);
  xor xor_7 (xor_7_out, B3, A3);
  xor xor_8 (S3, xor_7_out, or_3_out);
  and and_7 (and_7_out, xor_7_out, or_3_out);
  and and_8 (and_8_out, B3, B3);
  or or_4 (Carry, and_7_out, and_8_out);
endmodule

module Subtrator (
  input  B3,
  input  B2,
  input  B1,
  input  B0,
  input  A3,
  input  A2,
  input  A1,
  input  A0,
  input  C,
  output CARRY_OUT,
  output S3,
  output S2,
  output S1,
  output S0
);

  wire xor_1_out, xor_2_out, xor_3_out, xor_4_out;

  xor xor_1 (xor_1_out, B2, C);
  xor xor_2 (xor_2_out, B1, C);
  xor xor_3 (xor_3_out, B3, C);
  xor xor_4 (xor_4_out, B0, C);
  Somador somador_1 (
    .C(C), .A3(A3), .A2(A2), .A1(A1), .A0(A0), .B3(xor_3_out), .B2(xor_1_out), .B1(xor_2_out),
    .B0(xor_4_out), .S0(S0), .S1(S1), .S2(S2), .S3(S3), .Carry(CARRY_OUT));
endmodule

module Somador_Subtrator (
  input  in_1,
  input  in_2,
  input  in_3,
  input  in_4,
  input  in_5,
  input  in_6,
  input  in_7,
  input  in_8,
  input  \Operação ,
  output out_10,
  output out_11,
  output out_12,
  output out_13,
  output out_14
);

  Subtrator subtrator_1 (
    .C(\Operação ), .A3(in_1), .A2(in_2), .A1(in_3), .A0(in_4), .B3(in_5), .B2(in_6), .B1(in_7), .B0(in_8),
    .CARRY_OUT(out_10), .S3(out_11), .S2(out_12), .S1(out_13), .S0(out_14));

  // Notes on the sheet:
  //   A + B = S
  //   A - B = S
  //   1111 + 1111 = 1 1110
  //   1111 - 1111 = 1 0000
  //   Onde a Saída 1, que seria o “CARRY OUT”, seja ignorada
  //   Na soma será utilizada a saída “CARRY OUT”, para representar o resto da soma, por exemplo:
  //   , e como estamos subtraindo um número de 4 bits, o mesmo pode ser ignorada por exemplo:
  //   MODO DE FUNCIONAMENTO: 
  //   Na subtração não será utilizada a saída “CARRY OUT”, pois ela representa somente o resto da Soma,
  //   Soma: Quando a Porta “Operação” tiver em 0, o Circuito ira Somar os valores apresentados em Bits, entre A e B, Por exemplo:
  //   Subtração: Quando a Porta “Operação” tiver em 1, o Circuito ira Subtrair os valores apresentados em Bits, entre A e B, Por exemplo:
endmodule
