// Logisim project registrador.circ as structural Verilog: 1 circuit, main circuit main
module main (
  input  in_1,
  input  in_2,
  input  in_3,
  input  in_4,
  input  [1:0] in_5,
  input  in_6,
  input  in_7,
  output out_8,
  output out_9,
  output out_10,
  output out_11
);

  wire button_1_out, clock_1_out, multiplexer_1_out, multiplexer_2_out, multiplexer_3_out, multiplexer_4_out;

  Button button_1 (.out(button_1_out));
  Clock clock_1 (.out(clock_1_out));
  Multiplexer #(.select(2)) multiplexer_1 (
    .in0(out_8), .in1(out_9), .in2(in_7), .in3(in_1), .out(multiplexer_1_out), .sel(in_5));  // open: en
  Register #(.width(1)) register_1 (
    .D(multiplexer_1_out), .Q(out_8), .clk(clock_1_out), .clr(button_1_out));  // open: en
  Multiplexer #(.select(2)) multiplexer_2 (
    .in0(out_9), .in1(out_10), .in2(out_8), .in3(in_2), .out(multiplexer_2_out), .sel(in_5));  // open: en
  Register #(.width(1)) register_2 (
    .D(multiplexer_2_out), .Q(out_9), .clk(clock_1_out), .clr(button_1_out));  // open: en
  Register #(.width(1)) register_3 (
    .D(multiplexer_3_out), .Q(out_10), .clk(clock_1_out), .clr(button_1_out));  // open: en
  Multiplexer #(.select(2)) multiplexer_3 (
    .in0(out_10), .in1(out_11), .in2(out_9), .in3(in_3), .out(multiplexer_3_out), .sel(in_5));  // open: en
  Multiplexer #(.select(2)) multiplexer_4 (
    .in0(out_11), .in1(in_6), .in2(out_10), .in3(in_4), .out(multiplexer_4_out), .sel(in_5));  // open: en
  Register #(.width(1)) register_4 (
    .D(multiplexer_4_out), .Q(out_11), .clk(clock_1_out), .clr(button_1_out));  // open: en
endmodule
