// Logisim project memoria-ram.circ as structural Verilog: 1 circuit, main circuit main
module main (
  input  Habilita,
  input  limpa,
  input  [7:0] \Endereço ,
  input  W_R,
  input  habilita_2,
  input  in_6
);

  wire clock_1_out, not_1_out;
  wire [6:0] bit_extender_2_out, keyboard_1_data;
  wire [7:0] bit_extender_1_out, controlled_buffer_1_out, counter_1_q;

  Clock clock_1 (.out(clock_1_out));
  Keyboard keyboard_1 (.clk(clock_1_out), .re(Habilita), .clr(limpa), .data(keyboard_1_data));  // open: avail
  assign bit_extender_1_out = {{1{1'b0}}, keyboard_1_data};  // Bit_Extender bit_extender_1
  Counter counter_1 (.D(\Endereço ), .Q(counter_1_q), .clk(clock_1_out), .clr(limpa));  // open: load, count, carry
  TTY tty_1 (.data(bit_extender_2_out), .clk(clock_1_out), .we(not_1_out), .clr(limpa));
  assign controlled_buffer_1_out = W_R ? bit_extender_1_out : 8'bz;  // Controlled_Buffer controlled_buffer_1
  not not_1 (not_1_out, W_R);
  RAM ram_1 (
    .addr(counter_1_q), .data(controlled_buffer_1_out), .sel(habilita_2), .clk(clock_1_out), .ld(not_1_out),
    .clr(in_6));
  Bit_Extender #(.out_width(7)) bit_extender_2 (.in(controlled_buffer_1_out), .out(bit_extender_2_out));

  // Notes on the sheet:
  //   0 p/ leitura
endmodule
